# Fritzing sketch Sketch (saved by Fritzing 0.9.2b)
breadboards: 2

parts:
  Part1 = Arduino Uno (Rev3)
  Disp1 = LBT2088AH [part_number=LBT2088AH]
  U1 = MAX7219 [package=dil24]
  R1 = Resistor [tolerance=±5% resistance=220 package="0402 [SMD]"]
  R2 = Resistor [tolerance=±5% resistance=220 package="0402 [SMD]"]
  R3 = Resistor [tolerance=±5% resistance=220 package="0402 [SMD]"]

nets:
  N1: Part1.D10_PWM/SS, U1.LOAD
  N2: Part1.D11_PWM/MOSI, U1.CLK
  N3: Part1.D12/MISO, U1.DIN
  N4: Part1.5V, U1.SEGC, R1.Pin_1
  N5: Disp1.pin_16, U1.DIG0
  N6: U1.VCC, R3.Pin_0
  N7: R1.Pin_0, R2.Pin_1
  N8: R2.Pin_0, R3.Pin_1

notes:
  <-- 3x10000 ohm
